# Fritzing sketch ESQUEMA (saved by Fritzing 0.9.3b)
breadboards: 1

parts:
  Componente1 = Arduino Uno (Rev3)
  R2 = Resistor [tolerance=±5% resistance=220 package=THT]
  R3 = Resistor [tolerance=±5% resistance=220 package=THT]
  LED1 = LED - 5mm [color="Red (633nm)" package="5 mm [THT]"]
  LED2 = LED - 5mm [color="Red (633nm)" package="5 mm [THT]"]
  LED3 = LED - 5mm [color="Red (633nm)" package="5 mm [THT]"]
  U1 = SENSOR GAS [package=mq-3]
  R4 = Resistor [tolerance=±5% resistance=220 package=THT]
  J1 = Piezo Speaker

nets:
  N1: Componente1.A0, U1.A0
  N2: Componente1.D9_PWM, J1.VCC
  N3: Componente1.D2, R4.Pin_0
  N4: Componente1.D3_PWM, R3.Pin_0
  N5: Componente1.D4, R2.Pin_0
  5V: Componente1.5V, LED1.cathode, LED2.cathode, LED3.cathode, U1.VCC
  GND: Componente1.GND, U1.GND, J1.GND
  N6: R2.Pin_1, LED3.anode
  N7: R3.Pin_1, LED2.anode
  N8: LED1.anode, R4.Pin_1

notes:
  A0
  D0
  VCC
  GND

custom parts:
  SENSOR GAS: MQ-3 alcohol gas sensor .
  Piezo Speaker: Piezo
