# Fritzing sketch ESQUEMA2 (saved by Fritzing 0.9.3b)
breadboards: 1

parts:
  LCD1 = LCD screen
  Componente1 = Arduino Uno (Rev3)
  R1 = Rotary Potentiometer (Large) [maximum_resistance=100kΩ package=THT]

nets:
  VSS: LCD1.VSS, LCD1.R/W, LCD1.LED-, Componente1.GND, R1.leg1, R1.leg2
  VDD: LCD1.VDD, LCD1.LED+, Componente1.5V
  N1: LCD1.V0, R1.wiper
  N2: LCD1.RS, Componente1.D11_PWM/MOSI
  N3: LCD1.E, Componente1.D10_PWM/SS
  N4: LCD1.DB4, Componente1.D5_PWM
  N5: LCD1.DB5, Componente1.D6_PWM
  N6: LCD1.DB6, Componente1.D7
  N7: LCD1.DB7, Componente1.D8
